// Logisim project Q6.circ as structural Verilog: 1 circuit, main circuit main
module main (
);

  wire and_1_out, and_2_out, and_3_out, and_4_out, and_5_out, and_6_out, CLK, multiplexer_1_out, nand_1_out,
       not_1_out, or_1_out, or_2_out, w, y0, y1, y2;

  Multiplexer #(.enable("false")) multiplexer_1 (.in0(y2), .in1(not_1_out), .out(multiplexer_1_out), .sel(w));
  not not_1 (not_1_out, y2);
  nand nand_1 (nand_1_out, w, y2);
  and and_1 (and_1_out, ~w, ~y2, ~y1, ~y0);  // AND_Gate
  and and_2 (and_2_out, multiplexer_1_out, nand_1_out);
  LED led_1 (.in(y2));
  LED led_2 (.in(y1));
  or or_1 (or_1_out, and_1_out, and_2_out);
  LED led_3 (.in(w));
  LED led_4 (.in(y0));
  D_Flip_Flop d_ff_1 (.clk(CLK), .D(or_1_out), .Q(y0));  // open: Qn, preset, en, reset
  Clock clock_1 (.out(CLK));
  and and_3 (and_3_out, y0, nand_1_out);
  D_Flip_Flop d_ff_2 (.clk(CLK), .D(and_3_out), .Q(y1));  // open: Qn, preset, en, reset
  and and_4 (and_4_out, y1, nand_1_out);
  D_Flip_Flop d_ff_3 (.clk(CLK), .D(and_4_out), .Q(y2));  // open: Qn, preset, en, reset
  and and_5 (and_5_out, ~w, y2);  // AND_Gate
  or or_2 (or_2_out, and_5_out, and_6_out);
  and and_6 (and_6_out, w, ~y2);  // AND_Gate
  D_Flip_Flop d_ff_4 (.clk(CLK), .D(or_2_out), .Q(w));  // open: Qn, preset, en, reset
  // AND_Gate and_7 is placed but not wired
endmodule
