// Logisim project flip_flops.circ as structural Verilog: 1 circuit, main circuit main
module main (
  input  in_1,
  input  S,
  input  S_2,
  input  R,
  input  Clk,
  input  R_2,
  input  Clk_2,
  input  Clk_3,
  input  D,
  input  S_3,
  input  K,
  input  T,
  input  Clk_4,
  input  Clk_5,
  input  J,
  input  in_16,
  input  in_17,
  input  in_18
);

  wire and_1_out, and_2_out, and_3_out, and_4_out, and_5_out, and_6_out, and_7_out, and_8_out, clock_1_out,
       d_ff_1_q, d_ff_1_qn, nand_1_out, nand_2_out, nand_3_out, nand_4_out, nand_5_out, nand_6_out,
       nand_7_out, nand_8_out, nor_1_out, nor_2_out, nor_3_out, nor_4_out, nor_5_out, nor_6_out, nor_7_out,
       nor_8_out, nor_9_out, nor_10_out, not_1_out, not_2_out, not_3_out, s_r_ff_1_q, s_r_ff_1_qn,
       s_r_ff_2_q, s_r_ff_2_qn;

  and and_1 (and_1_out, R_2, Clk_2);
  and and_2 (and_2_out, Clk_2, S_3);
  and and_3 (and_3_out, nor_5_out, K, Clk_4);
  and and_4 (and_4_out, Clk_4, J, nor_6_out);
  S_R_Flip_Flop s_r_ff_1 (
    .S(in_16), .clk(in_18), .R(in_17), .Q(s_r_ff_1_q), .Qn(s_r_ff_1_qn));  // open: preset, reset, en
  not not_1 (not_1_out, in_18);
  nor nor_1 (nor_1_out, in_1, nor_2_out);
  nor nor_2 (nor_2_out, nor_1_out, S_2);
  nor nor_3 (nor_3_out, and_1_out, nor_4_out);
  nor nor_4 (nor_4_out, nor_3_out, and_2_out);
  nor nor_5 (nor_5_out, and_3_out, nor_6_out);
  nor nor_6 (nor_6_out, nor_5_out, and_4_out);
  S_R_Flip_Flop s_r_ff_2 (
    .S(s_r_ff_1_q), .clk(not_1_out), .R(s_r_ff_1_qn), .Q(s_r_ff_2_q), .Qn(s_r_ff_2_qn));  // open: preset, reset, en
  not not_2 (not_2_out, T);
  nand nand_1 (nand_1_out, S, nand_2_out);
  nand nand_2 (nand_2_out, nand_1_out, R);
  not not_3 (not_3_out, nor_8_out);
  and and_5 (and_5_out, nor_9_out, T, Clk_5);
  and and_6 (and_6_out, Clk_5, not_2_out, nor_10_out);
  and and_7 (and_7_out, nor_8_out, Clk_3);
  and and_8 (and_8_out, Clk_3, not_3_out);
  nor nor_7 (nor_7_out, and_7_out, nor_8_out);
  nor nor_8 (nor_8_out, nor_7_out, and_8_out);
  nor nor_9 (nor_9_out, and_5_out, nor_10_out);
  nor nor_10 (nor_10_out, nor_9_out, and_6_out);
  nand nand_3 (nand_3_out, nand_6_out, nand_4_out);
  nand nand_4 (nand_4_out, nand_3_out, Clk);
  nand nand_5 (nand_5_out, nand_4_out, Clk, nand_6_out);
  nand nand_6 (nand_6_out, nand_5_out, D);
  Clock clock_1 (.out(clock_1_out));
  D_Flip_Flop d_ff_1 (.clk(clock_1_out), .D(d_ff_1_qn), .Q(d_ff_1_q), .Qn(d_ff_1_qn));  // open: preset, en, reset
  nand nand_7 (nand_7_out, nand_4_out, nand_8_out);
  nand nand_8 (nand_8_out, nand_7_out, nand_5_out);

  // Notes on the sheet:
  //   R
  //   RS Flip Flop with Clock
  //   JK Flip Flop
  //   JK flip flop is used, or an edge-triggered configuration is used
  //   Master-Slave JK Flip Flop
  //   *Oscillations occur when clock pulse is >= gate delay. Hence
  //   JK flip flops are never constructed like this. Either a master-slave
  //   RS Flip Flops
  //   Q
  //   Q'
  //   Q
  //   Q'
  //   Q
  //   Q'
  //   D
  //   Note that this has the inital
  //   state of input pins as 1 
  //   D Flip Flop
  //   *Morris Mano & Class uses a diff. impl with NAND's
  //   T flip flop
  //   Q
  //   Q'
  //   Same restriction as JK does not apply, as J and K are never 1 simultaneously.
  //   Q
  //   Q'
  //   Q
  //   Q'
  //   D Flip Flop
  //   Positive edge triggered
  //   Q
  //   Q'
endmodule
