// Logisim project registers.circ as structural Verilog: 1 circuit, main circuit main
module main (
  input  Clk,
  input  D,
  input  in_3,
  input  in_4,
  input  in_5,
  input  in_6,
  input  Clk_2,
  input  in_8,
  input  in_9,
  input  in_10,
  input  in_11,
  input  in_12,
  input  in_13
);

  wire and_1_out, and_2_out, and_3_out, and_4_out, and_5_out, and_6_out, and_7_out, and_8_out, clock_1_out,
       d_ff_1_q, d_ff_2_q, d_ff_3_q, d_ff_4_q, d_ff_5_q, d_ff_6_q, d_ff_7_q, d_ff_8_q, d_ff_9_q, d_ff_10_q,
       d_ff_11_q, d_ff_12_q, not_1_out, or_1_out, or_2_out, or_3_out, or_4_out;

  Clock clock_1 (.out(clock_1_out));
  and and_1 (and_1_out, in_8, not_1_out);
  D_Flip_Flop d_ff_1 (.clk(Clk), .D(D), .Q(d_ff_1_q));  // open: Qn, preset, en, reset
  D_Flip_Flop d_ff_2 (.clk(Clk_2), .D(in_3), .Q(d_ff_2_q));  // open: Qn, preset, en, reset
  LED led_1 (.in(d_ff_3_q));
  D_Flip_Flop d_ff_3 (.clk(clock_1_out), .D(or_1_out), .Q(d_ff_3_q));  // open: Qn, preset, en, reset
  or or_1 (or_1_out, and_1_out, and_2_out);
  and and_2 (and_2_out, in_9, in_10);
  not not_1 (not_1_out, in_9);
  or or_2 (or_2_out, and_3_out, and_4_out);
  and and_3 (and_3_out, d_ff_3_q, not_1_out);
  and and_4 (and_4_out, in_9, in_11);
  D_Flip_Flop d_ff_4 (.clk(Clk), .D(d_ff_1_q), .Q(d_ff_4_q));  // open: Qn, preset, en, reset
  D_Flip_Flop d_ff_5 (.clk(Clk_2), .D(in_4), .Q(d_ff_5_q));  // open: Qn, preset, en, reset
  LED led_2 (.in(d_ff_6_q));
  D_Flip_Flop d_ff_6 (.clk(clock_1_out), .D(or_2_out), .Q(d_ff_6_q));  // open: Qn, preset, en, reset
  or or_3 (or_3_out, and_5_out, and_6_out);
  and and_5 (and_5_out, d_ff_6_q, not_1_out);
  D_Flip_Flop d_ff_7 (.clk(Clk), .D(d_ff_4_q), .Q(d_ff_7_q));  // open: Qn, preset, en, reset
  D_Flip_Flop d_ff_8 (.clk(Clk_2), .D(in_5), .Q(d_ff_8_q));  // open: Qn, preset, en, reset
  LED led_3 (.in(d_ff_9_q));
  D_Flip_Flop d_ff_9 (.clk(clock_1_out), .D(or_3_out), .Q(d_ff_9_q));  // open: Qn, preset, en, reset
  and and_6 (and_6_out, in_9, in_12);
  D_Flip_Flop d_ff_10 (.clk(Clk), .D(d_ff_7_q), .Q(d_ff_10_q));  // open: Qn, preset, en, reset
  D_Flip_Flop d_ff_11 (.clk(Clk_2), .D(in_6), .Q(d_ff_11_q));  // open: Qn, preset, en, reset
  D_Flip_Flop d_ff_12 (.clk(clock_1_out), .D(or_4_out), .Q(d_ff_12_q));  // open: Qn, preset, en, reset
  or or_4 (or_4_out, and_7_out, and_8_out);
  and and_7 (and_7_out, d_ff_9_q, not_1_out);
  and and_8 (and_8_out, in_9, in_13);
  LED led_4 (.in(d_ff_12_q));
  // NOT_Gate not_2 is placed but not wired

  // Notes on the sheet:
  //   D
  //   Serial In Parallel Out Shift Register
  //   S3
  //   Parallel In Parallel Out Register
  //   S3
  //   S2
  //   S2
  //   S1
  //   S1
  //   S0
  //   S0
endmodule
